// Digital circuit CPU.dig as structural Verilog
module CPU (
  input  clock
);

  wire branchCtl_taken, execution_unit_zero;
  wire [1:0] rf_p3;
  wire [10:0] MainControl_d;
  wire [15:0] bitextender_1_out, branch_unit_r, DMemory_d, execution_unit_r, IMemory_d, multiplexer_1_out,
       multiplexer_2_out, pc_incrementer_r, PC_q, rf_p4, rf_p7, rf_p8, shift_left_1_1_out;

  D_FF #(.Bits(16)) PC (.D(multiplexer_1_out), .C(~clock), .Q(PC_q));  // open: nQ
  Multiplexer #(.Bits(16)) multiplexer_1 (
    .sel(branchCtl_taken), .in_0(pc_incrementer_r), .in_1(branch_unit_r), .out(multiplexer_1_out));
  ALU pc_incrementer (.r(pc_incrementer_r), .a(PC_q), .b(16'h2), .s(4'b0010));  // open: zero, overflow
  ROM #(.AddrBits(16), .Bits(16)) IMemory (.A(PC_q), .sel(1'b1), .D(IMemory_d));
  ROM #(.AddrBits(4), .Bits(11)) MainControl (.A(IMemory_d[15:12]), .sel(1'b1), .D(MainControl_d));
  // reg_file rf: pin names not known; wires that end beside it: IMemory_d[11:10], IMemory_d[9:8], rf_p3, rf_p4, MainControl_d[7], clock, rf_p7, rf_p8
  BitExtender bitextender_1 (.in(IMemory_d[7:0]), .out(bitextender_1_out));
  shift_left_1 shift_left_1_1 (.in(bitextender_1_out), .out(shift_left_1_1_out));
  Multiplexer #(.Bits(16)) multiplexer_2 (
    .sel(MainControl_d[9]), .in_0(rf_p8), .in_1(bitextender_1_out), .out(multiplexer_2_out));
  Multiplexer #(.Bits(2)) multiplexer_3 (
    .sel(MainControl_d[10]), .in_0(IMemory_d[9:8]), .in_1(IMemory_d[7:6]), .out(rf_p3));
  ALU branch_unit (
    .r(branch_unit_r), .a(pc_incrementer_r), .b(shift_left_1_1_out), .s(4'b0010));  // open: zero, overflow
  ALU execution_unit (
    .zero(execution_unit_zero), .r(execution_unit_r), .a(rf_p7), .b(multiplexer_2_out), .s(MainControl_d[3:0]));  // open: overflow
  BranchControl branchCtl (
    .Taken(branchCtl_taken), .BEQ(MainControl_d[5]), .BNE(MainControl_d[4]), .Zero(execution_unit_zero));
  BlockRAMDualPort #(.AddrBits(16), .Bits(16)) DMemory (
    .A(execution_unit_r), .Din(rf_p8), .str(MainControl_d[6]), .C(clock), .D(DMemory_d));
  Multiplexer #(.Bits(16)) multiplexer_4 (
    .sel(MainControl_d[8]), .in_0(execution_unit_r), .in_1(DMemory_d), .out(rf_p4));

  // Notes on the sheet:
  //   NextPC
  //   muxBranch
  //   contents of IMemory (hex, n*v repeats v):
  //   7407,0,7803,0,9100,0,9202,0,8100,0,8202,0,66c0,0,ac02,0,9102,0
  //   ,9200,0,8100,0,8202,0,4a80,0,7a01,0,6c0
  //   PCplus2
  //   IR
  //   IF/ID
  //   contents of MainControl (hex, n*v repeats v):
  //   482,486,480,481,48c,48d,487,282,382,242,26,16
  //   BEQ
  //   BNE
  //   RegWrite
  //   MemtoReg
  //   MemWrite
  //   RegDst
  //   ALUSrc
  //   ALUctl
  //   A
  //   RD2
  //   SignExtend
  //   ID/EX
  //   muxData
  //   B
  //   muxReg
  //   WR
  //   Target
  //   EX/MA
  //   Zero
  //   ALUOut
  //   BranchTaken
  //   MA/WB
  //   muxWriteReg
  //   WD
endmodule
